# Fritzing sketch MID_5 (saved by Fritzing 0.9.3b)

parts:
  元件1 = node32s
  LED1 = RGB LED (com. cathode, rgb) [package="5 mm [THT]"]

nets:
  N1: 元件1.GND, LED1.common_cathode
  N2: 元件1.IO5, LED1.red_anode
  N3: 元件1.IO17, LED1.green_anode
  N4: 元件1.IO16, LED1.blue_anode
